# Fritzing sketch MMM (saved by Fritzing 1.0.6)
circuit board: 3.99999cm x 11cm
breadboards: 3

parts:
  CV1 = PJ-301M [part_number=PJ-301M]
  J3 = shrouded pin header, 16 pins [form="♂ (shrouded male)"]
  CV5 = PJ-301M [part_number=PJ-301M]
  CV6 = PJ-301M [part_number=PJ-301M]
  CV2 = PJ-301M [part_number=PJ-301M]
  Left = PJ-301M [part_number=PJ-301M]
  CV4 = PJ-301M [part_number=PJ-301M]
  Right = PJ-301M [part_number=PJ-301M]
  3_3k = Resistor [tolerance=±1% power=0.25W resistance=3.3k package=THT]
  RE1 = Rotary Encoder [package=THT]
  OLED = OLED Mono 0.56 inch blue or white
  RE3 = Rotary Encoder [package=THT]
  RE2 = Rotary Encoder [package=THT]
  RE4 = Rotary Encoder [package=THT]
  J10 = female pin header, 20 pins [form="♀ (female)"]
  J11 = female pin header, 3 pins [form="♀ (female)"]
  104 = Ceramic Capacitor [capacitance=100nF voltage=35V package="100 mil [THT, multilayer]"]
  4001 = Rectifier Diode [part_number=1N4001 package="300 mil [THT]"]
  100uF = Electrolytic Capacitor [capacitance=0.1mF voltage=35V package="100 mil [THT, electrolytic]"]
  J7 = female pin header, 9 pins [form="♀ (female)"]
  J8 = female pin header, 6 pins [form="♀ (female)"]
  3_3k_2 = Resistor [tolerance=±1% power=0.25W resistance=3.3k package=THT]
  3_3k_3 = Resistor [tolerance=±1% power=0.25W resistance=3.3k package=THT]
  3_3k_4 = Resistor [tolerance=±1% power=0.25W resistance=3.3k package=THT]
  3_3k_5 = Resistor [tolerance=±1% power=0.25W resistance=3.3k package=THT]
  J9 = female pin header, 20 pins [form="♀ (female)"]
  CV3 = PJ-301M [part_number=PJ-301M]
  3_3k_6 = Resistor [tolerance=±1% power=0.25W resistance=3.3k package=THT]
  3_3k_7 = Resistor [tolerance=±1% power=0.25W resistance=3.3k package=THT]
  3_3k_8 = Resistor [tolerance=±1% power=0.25W resistance=3.3k package=THT]
  3_3k_9 = Resistor [tolerance=±1% power=0.25W resistance=3.3k package=THT]
  3_3k_10 = Resistor [tolerance=±1% power=0.25W resistance=3.3k package=THT]
  3_3k_11 = Resistor [tolerance=±1% power=0.25W resistance=3.3k package=THT]
  LM7805 = Voltage Regulator [package=to220-igo]
  3_3k_12 = Resistor [tolerance=±1% power=0.25W resistance=3.3k package=THT]
  3_3k1 = Resistor [tolerance=±1% power=0.25W resistance=3.3k package=THT]
  3_3k_13 = Resistor [tolerance=±1% power=0.25W resistance=3.3k package=THT]
  3_3k_14 = Resistor [tolerance=±1% power=0.25W resistance=3.3k package=THT]
  3_3k_15 = Resistor [tolerance=±1% power=0.25W resistance=3.3k package=THT]
  3_3k_16 = Resistor [tolerance=±1% power=0.25W resistance=3.3k package=THT]
  3_3k_17 = Resistor [tolerance=±1% power=0.25W resistance=3.3k package=THT]
  104_2 = Ceramic Capacitor [capacitance=100nF voltage=35V package="200 mil [THT, multilayer]"]

nets (from the schematic view):
  GND: CV1.Pin_1, J3.pin2, J3.pin3, J3.pin4, J3.pin13, J3.pin14, J3.pin15, CV5.Pin_1, CV6.Pin_1, CV2.Pin_1, CV4.Pin_1, RE1.GND, RE1.SW-1, OLED.GND, RE3.GND, RE3.SW-1, RE2.GND, RE2.SW-1, RE4.GND, RE4.SW-1, J10.pin10, J10.pin20, J11.pin3, 104.0, 100uF.-, J8.pin1, J8.pin5, 3_3k_3.Pin_0, 3_3k_5.Pin_1, J9.pin10, J9.pin20, CV3.Pin_1, 3_3k_6.Pin_1, 3_3k_8.Pin_0, 3_3k_10.Pin_0, LM7805.GND, 3_3k_12.Pin_1, 3_3k1.Pin_1, 3_3k_13.Pin_1, 3_3k_14.Pin_0, 3_3k_15.Pin_1, 3_3k_16.Pin_0, 3_3k_17.Pin_1, 104_2.0
  N1: CV1.Pin_3, 3_3k.Pin_0
  N2: J3.pin1, J3.pin16
  9V: J3.pin5, J3.pin6, J3.pin11, J3.pin12, 4001.anode
  N3: J3.pin7, J3.pin10
  N4: J3.pin8, J3.pin9
  N5: CV5.Pin_3, 3_3k_4.Pin_0
  N6: CV6.Pin_3, 3_3k_11.Pin_0
  N7: CV2.Pin_3, 3_3k_2.Pin_0
  N8: Left.Pin_1, J7.pin8
  N9: Left.Pin_3, J7.pin9
  N10: CV4.Pin_3, 3_3k_9.Pin_0
  N11: Right.Pin_1, J7.pin6
  N12: Right.Pin_3, J7.pin7
  CV1: 3_3k.Pin_1, J9.pin12, 3_3k_12.Pin_0, 3_3k1.Pin_0
  1A: RE1.Pin-A, J9.pin6
  1B: RE1.Pin-B, J9.pin7
  SW1: RE1.SW-2, J9.pin8
  SDA1: OLED.SDA, J10.pin6
  SCL1: OLED.SCL, J10.pin7
  3v+: OLED.VCC, J10.pin1, J10.pin11, J8.pin6, J9.pin1, J9.pin11, 104_2.1
  3A: RE3.Pin-A, J10.pin4
  3B: RE3.Pin-B, J10.pin5
  SW3: RE3.SW-2, J10.pin9
  2A: RE2.Pin-A, J10.pin15
  2B: RE2.Pin-B, J10.pin14
  SW2: RE2.SW-2, J9.pin9
  4A: RE4.Pin-A, J10.pin12
  4B: RE4.Pin-B, J10.pin13
  SW4: RE4.SW-2, J10.pin18
  SDA2: J10.pin16, J8.pin2
  SCL2: J10.pin17, J8.pin4
  DIN: J10.pin19, J8.pin3
  5v+: J11.pin2, LM7805.OUT
  N13: 104.1, 4001.cathode, 100uF.+, LM7805.IN
  Mute: J7.pin3, J9.pin19
  CV2: 3_3k_2.Pin_1, 3_3k_3.Pin_1, J9.pin13, 3_3k_16.Pin_1
  CV5: 3_3k_4.Pin_1, 3_3k_5.Pin_0, J9.pin16, 3_3k_13.Pin_0
  CV3: J9.pin14, 3_3k_6.Pin_0, 3_3k_7.Pin_1, 3_3k_15.Pin_0
  CV4: J9.pin15, 3_3k_8.Pin_1, 3_3k_9.Pin_1, 3_3k_17.Pin_0
  CV6: J9.pin18, 3_3k_10.Pin_1, 3_3k_11.Pin_1, 3_3k_14.Pin_1
  N14: CV3.Pin_3, 3_3k_7.Pin_0

notes:
  marvelous
  jlcjlcjlcjlcjlc
  All dividers with load on the inputs are
  3.3k (4.7k is also good)
  to cover 10v input (scaled to 3.3.
  3.3k divider + 4.7k load
  gives a bit more range and is safe to 9volts
  blueprint@poetaster.de 2026
  upsidedown rp2350b
  (on bottom)
  +3.3 - VBUS
  GPIO32 - VSYS
  GPIO33 - GND
  GPIO34
  GPIO35
  GPIO36
  GPIO37
  GPIO38
  GPIO39
  GND
  +3.3
  GPIO40
  GPIO41
  GPIO42
  GPIO43
  GPIO44
  GPIO45
  GPIO46
  GPIO47
  GND
  upsidedown rp2350b
  +3.3
  GPIO00
  GPIO01
  GPIO02
  GPIO03
  GPIO04
  GPIO05
  GPIO06
  GPIO07
  GND
  +3.3
  GPIO08
  GPIO09
  GPIO10
  GPIO11
  GPIO12
  GPIO13
  GPIO14
  GPIO15
  GND

custom parts:
  PJ-301M: Phone power jack.
  Rotary Encoder: Rotary Encoder with push button
  OLED Mono 0.56 inch blue or white: OLED, I2C 3.3V - 5V Blue and White text versions
