# Fritzing sketch marvelous-desktop (saved by Fritzing 1.0.6)
circuit board: 8.73592cm x 6.43364cm
breadboards: 3

parts:
  220 = Resistor [tolerance=±1% power=0.25W resistance=3.3k package=THT]
  RE1 = Rotary Encoder [package=THT]
  OLED = OLED Mono 0.56 inch blue or white
  RE3 = Rotary Encoder [package=THT]
  RE2 = Rotary Encoder [package=THT]
  RE4 = Rotary Encoder [package=THT]
  220_2 = Resistor [tolerance=±1% power=0.25W resistance=220 package=THT]
  220_3 = Resistor [tolerance=±1% power=0.25W resistance=220 package=THT]
  220_4 = Resistor [tolerance=±1% power=0.25W resistance=220 package=THT]
  220_5 = Resistor [tolerance=±1% power=0.25W resistance=220 package=THT]
  220_6 = Resistor [tolerance=±1% power=0.25W resistance=3.3k package=THT]
  J9 = female pin header, 20 pins [form="♀ (female)"]
  J10 = female pin header, 20 pins [form="♀ (female)"]
  CV1 = double row female pin header, 4 pins [form="♀ (female)"]
  CV2 = double row female pin header, 4 pins [form="♀ (female)"]
  CV3 = double row female pin header, 4 pins [form="♀ (female)"]
  CV4 = double row female pin header, 4 pins [form="♀ (female)"]
  CV6 = double row female pin header, 4 pins [form="♀ (female)"]
  CV5 = double row female pin header, 4 pins [form="♀ (female)"]
  Trig = double row female pin header, 4 pins [form="♀ (female)"]
  Right = female pin header, 2 pins [form="♀ (female)"]
  Left = female pin header, 2 pins [form="♀ (female)"]
  J8 = female pin header, 6 pins [form="♀ (female)"]
  J7 = female pin header, 9 pins [form="♀ (female)"]
  220_7 = Resistor [tolerance=±5% power=0.25W resistance=220 package=THT]
  D4149 = Diode [package=diode-1n4148]
  104 = Ceramic Capacitor [capacitance=100nF voltage=35V package="200 mil [THT, multilayer]"]
  6N138 = IC, DIP package, 8 pins [chip_label=6N138]
  J11 = 3.5mm Audio Jack-wq-pj320b.fzpz [package=audio-jack-3.5mm-smd]
  100uF = Electrolytic Capacitor [capacitance=0.1mF voltage=35V package="100 mil [THT, electrolytic]"]
  220_8 = Resistor [tolerance=±1% power=0.25W resistance=220 package=THT]
  4_7k = Resistor [tolerance=±5% power=0.25W resistance=4.7k package=THT]
  3_3v = DIODE-ZENER [package=diode-zener]
  3_3v_2 = DIODE-ZENER [package=diode-zener]
  3_3v_3 = DIODE-ZENER [package=diode-zener]
  3_3v_4 = DIODE-ZENER [package=diode-zener]
  3_3v_5 = DIODE-ZENER [package=diode-zener]
  3_3v_6 = DIODE-ZENER [package=diode-zener]
  3_3v_7 = DIODE-ZENER [package=diode-zener]
  3_3v_8 = DIODE-ZENER [package=diode-zener]
  3_3v_9 = DIODE-ZENER [package=diode-zener]
  3_3v_10 = DIODE-ZENER [package=diode-zener]
  3_3v_11 = DIODE-ZENER [package=diode-zener]
  3_3v_12 = DIODE-ZENER [package=diode-zener]
  104_2 = Ceramic Capacitor [capacitance=100nF voltage=35V package="200 mil [THT, multilayer]"]
  3_3v_13 = DIODE-ZENER [package=diode-zener]
  3_3v2 = DIODE-ZENER [package=diode-zener]

nets:
  N1: 220.Pin_0, CV1.pin1, CV1.pin2, CV1.pin3, CV1.pin4
  CV1: 220.Pin_1, J9.pin14, 3_3v_5.C, 3_3v_6.A
  1A: RE1.Pin-A, J9.pin2
  GND: RE1.GND, RE1.SW-1, OLED.GND, RE3.GND, RE3.SW-2, RE2.GND, RE2.SW-2, RE4.GND, RE4.SW-1, J9.pin20, J10.pin10, J10.pin20, J8.pin1, J8.pin5, 104.1, 6N138.pin5, J11.pin_4, 100uF.-, 3_3v_2.A, 3_3v_3.A, 3_3v_4.A, 3_3v_5.A, 3_3v_9.A, 3_3v_11.A, 104_2.0, 3_3v2.A
  1B: RE1.Pin-B, J9.pin3
  SW1: RE1.SW-2, J9.pin4
  SDA1: OLED.SDA, J10.pin6
  SCL1: OLED.SCL, J10.pin7
  3v+: OLED.VCC, J9.pin1, J9.pin11, J10.pin1, J10.pin11, J8.pin6, 104.0, 6N138.pin8, 100uF.+, 4_7k.Pin_0, 3_3v.C, 3_3v_6.C, 3_3v_7.C, 3_3v_8.C, 3_3v_10.C, 3_3v_12.C, 104_2.1, 3_3v_13.C
  3A: RE3.Pin-A, J9.pin9
  3B: RE3.Pin-B, J9.pin12
  SW3: RE3.SW-1, J9.pin8
  2A: RE2.Pin-A, J9.pin6
  2B: RE2.Pin-B, J9.pin7
  SW2: RE2.SW-1, J9.pin5
  4A: RE4.Pin-A, J10.pin8
  4B: RE4.Pin-B, J10.pin9
  SW4: RE4.SW-2, J10.pin4
  N2: 220_2.Pin_0, CV2.pin1, CV2.pin2, CV2.pin3, CV2.pin4
  CV2: 220_2.Pin_1, J9.pin15, 3_3v_4.C, 3_3v_8.A
  N3: 220_3.Pin_0, CV5.pin1, CV5.pin2, CV5.pin3, CV5.pin4
  CV5: 220_3.Pin_1, J9.pin18, 3_3v_3.C, 3_3v_7.A
  N4: 220_4.Pin_0, CV3.pin1, CV3.pin2, CV3.pin3, CV3.pin4
  CV3: 220_4.Pin_1, J9.pin16, 3_3v.A, 3_3v_2.C
  N5: 220_5.Pin_0, CV4.pin1, CV4.pin2, CV4.pin3, CV4.pin4
  CV4: 220_5.Pin_1, J9.pin17, 3_3v_11.C, 3_3v_12.A
  N6: 220_6.Pin_0, CV6.pin1, CV6.pin2, CV6.pin3, CV6.pin4
  CV6: 220_6.Pin_1, J9.pin19, 3_3v_9.C, 3_3v_10.A
  TR: J9.pin13, 220_8.Pin_0, 3_3v_13.A, 3_3v2.C
  Midi: J10.pin3, 6N138.pin6, 4_7k.Pin_1
  SDA2: J10.pin12, J8.pin2
  SCL2: J10.pin13, J8.pin4
  DIN: J10.pin14, J8.pin3
  Mute: J10.pin15, J7.pin3
  N7: Trig.pin1, Trig.pin2, Trig.pin3, Trig.pin4, 220_8.Pin_1
  N8: Right.pin1, J7.pin7
  N9: Right.pin2, J7.pin6
  N10: Left.pin1, J7.pin9
  N11: Left.pin2, J7.pin8
  N12: 220_7.Pin_0, D4149.C, 6N138.pin2
  N13: 220_7.Pin_1, J11.pin_2
  N14: D4149.A, 6N138.pin3, J11.Pin_3

notes:
  marvelous MI
  jlcjlcjlcjlcjlc
  [write your note here]14.7k / 5.6k - 3.3
  8.2k / 3.1k -3.3
  vin 12 3.38 out
  A 5.6k, B 1.1k, C 5.6k
  vin 10 (ref 3.3) 3.284 out
  A 10k, B 4.7k, C. 3.3k
  primary 8.2k -.- 5.6k
  blueprint@poetaster.de
  olimex pico2xxl
  5102a DAC module

custom parts:
  Rotary Encoder: Rotary Encoder with push button
  OLED Mono 0.56 inch blue or white: OLED, I2C 3.3V - 5V Blue and White text versions
  3.5mm Audio Jack-wq-pj320b.fzpz: 3.5mm Audio Jack WQP-PJ320B is a SMD jack, dia 1/8 inch, female, right angle and through hole.
